# Fritzing sketch Arduino-WiFi-Fencing-Scoring-detection-PORT-wiring (saved by Fritzing 0.9.3b)

parts:
  WeMos_D1_Mini1 = WeMos D1 Mini
  Connected_LED = LED - 5mm [color="Green (560nm)" package="5 mm [THT]"]
  Hit_LED = LED - 5mm [color="Red (635nm)" package="5 mm [THT]"]
  R1 = Resistor [tolerance=±5% resistance=330 package=THT]
  R2 = Resistor [tolerance=±5% resistance=330 package=THT]
  R3 = Resistor [tolerance=±5% resistance=100k package="0805 [SMD]"]
  Fencer_Tip = Pushbutton [package="[THT]"]

nets:
  N1: WeMos_D1_Mini1.5V, R1.Pin_0, R2.Pin_0, Fencer_Tip.Pin_3, Fencer_Tip.Pin_4
  N2: WeMos_D1_Mini1.D0, R3.Pin_0, Fencer_Tip.Pin_1
  N3: WeMos_D1_Mini1.D3, Hit_LED.cathode
  N4: WeMos_D1_Mini1.D4, Connected_LED.cathode
  N5: WeMos_D1_Mini1.G, R3.Pin_1
  N6: Connected_LED.anode, R2.Pin_1
  N7: Hit_LED.anode, R1.Pin_1
